# Fritzing sketch Greenhouse (saved by Fritzing 0.9.3b)
circuit board: 5.13495cm x 4.64152cm
breadboards: 1

parts:
  Raspberry_Pi_1 = Raspberry Pi 3 [part_number=RPI-3-V1.2]
  SparkFun_CSS811_Breakout1 = SparkFun_CSS811_Breakout [part_number=14193]
  OLED = Header 4 [package=molex-1x4_lock]
  Temp/Humid = Header 4 [package=molex-1x4_lock]

nets:
  3V3: Raspberry_Pi_1.3v3, SparkFun_CSS811_Breakout1.3.3V, OLED.2, Temp/Humid.2
  N1: Raspberry_Pi_1.GPIO2, SparkFun_CSS811_Breakout1.SDA, OLED.4, Temp/Humid.4
  N2: Raspberry_Pi_1.GPIO3, SparkFun_CSS811_Breakout1.SCL, OLED.3, Temp/Humid.3
  GND: Raspberry_Pi_1.GND, SparkFun_CSS811_Breakout1.!WAKE, SparkFun_CSS811_Breakout1.GND, OLED.1, Temp/Humid.1

notes:
  Colin, Kenneth, Princess

custom parts:
  SparkFun_CSS811_Breakout: The CCS811 Air Quality Breakout is a digital gas sensor solution that senses a wide range of Total Volatile Organic Compounds (TVOCs), including equivalent carbon dioxide (eCO2) and metal oxide (MOX) levels. VOCs are often categorized as pollutants and/or sensory irritants and can come from a variety of sources like construction materials (paint, carpet, etc.), machines (copiers, processors,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
